# Fritzing sketch LEDBedBand (saved by Fritzing 0.9.0b)
circuit board: 4.9cm x 4.2cm
breadboards: 1

parts:
  MOSFET_G = Basic FET N-Channel [package="TO220 [THT]"]
  MOSFET_R = Basic FET N-Channel [package="TO220 [THT]"]
  P_R2 = PHOTOCELL [package=photocell-kit]
  LED_Strip = RGB LED - (4 legs) [package="5 mm [THT]"]
  P_R1 = Resistor [tolerance=±5% resistance=10k package=THT]
  PIR1 = PIR sensor
  PIR2 = PIR sensor
  Arduino_Nano = Arduino Nano (Rev3.0)
  MOSFET_B = Basic FET N-Channel [package="TO220 [THT]"]
  V_R1 = Resistor [tolerance=±5% resistance=1M package=THT]
  V_R2 = Resistor [tolerance=±5% resistance=680k package=THT]
  VIN = female pin header, 2 pins [form="♀ (female)"]
  VUP_IN = female pin header, 2 pins [form="♀ (female)"]
  VUP_OUT = female pin header, 2 pins [form="♀ (female)"]
  L_B = female pin header, 1 pin [form="♀ (female)"]
  L_G = female pin header, 1 pin [form="♀ (female)"]
  L_R = female pin header, 1 pin [form="♀ (female)"]

nets:
  N1: MOSFET_G.gate, Arduino_Nano.D9
  N2: MOSFET_G.drain, LED_Strip.green_cathode, L_G.pin1
  GND: MOSFET_G.source, MOSFET_R.source, P_R2.P$2, PIR1.GND, PIR2.GND, Arduino_Nano.GND, MOSFET_B.source, V_R2.Pin_1, VIN.pin2, VUP_IN.pin2, VUP_OUT.pin2
  N3: MOSFET_R.gate, Arduino_Nano.D6
  N4: MOSFET_R.drain, LED_Strip.red_cathode, L_R.pin1
  N5: P_R2.P$1, P_R1.Pin_0, Arduino_Nano.A0
  N6: LED_Strip.common_anode, Arduino_Nano.VIN, V_R1.Pin_0, VIN.pin1, VUP_IN.pin1, VUP_OUT.pin1
  N7: LED_Strip.blue_cathode, MOSFET_B.drain, L_B.pin1
  V5V: P_R1.Pin_1, PIR1.VDD, PIR2.VDD, Arduino_Nano.5V
  N8: PIR1.SIG, Arduino_Nano.D2
  N9: PIR2.SIG, Arduino_Nano.D3
  N10: Arduino_Nano.D5, MOSFET_B.gate
  N11: Arduino_Nano.A2, V_R1.Pin_1, V_R2.Pin_0

notes:
  R
  G
  B
  12V Step-Up Converter here
  Battery here
  GND
  VIN
  NC
  LEDBedBand v1.1
  https://github.com/anvo/ledbedband
  Arduino Nano
